# Fritzing sketch Schematic (saved by Fritzing 0.8.7b)
breadboards: 1

parts:
  Part1 = Arduino Uno (Rev3) - ICSP
  LED1 = LEDs [package=led10mm]
  LED2 = LEDs [package=led10mm]
  LED3 = LEDs [package=led10mm]
  LED4 = LEDs [package=led10mm]

nets:
  N1: Part1.D8, LED2.A
  N2: Part1.D9_PWM, LED1.A
  N3: Part1.GND, LED1.C, LED2.C, LED3.C, LED4.C
  N4: Part1.D6_PWM, LED4.A
  N5: Part1.D7, LED3.A
