# Fritzing sketch Receiver Schematic (saved by Fritzing 0.8.7b)

parts:
  NRF24L1 = NRF24L01
  Part1 = Arduino Nano (Rev3.0)
  LED1 = LED - 5mm [color="Red (633nm)" package="5 mm [THT]"]
  R1 = Resistor [tolerance=±10% resistance=220 package=THT]
  S1 = Pushbutton [package="[THT]"]
  R2 = Resistor [part_number=2 package="2010 [SMD]"]

nets:
  VCC: NRF24L1.VCC, Part1.3V3
  N1: NRF24L1.CSN, Part1.D10
  N2: NRF24L1.MOSI, Part1.D11/MOSI
  GND: NRF24L1.GND, Part1.GND, LED1.cathode
  N3: NRF24L1.CE, Part1.D9
  N4: NRF24L1.SCK, Part1.D13/SCK
  N5: NRF24L1.MISO, Part1.D12/MISO
  N6: Part1.D2, R1.Pin_1
  N7: Part1.D3, R2.Pin_1
  N8: S1.Pin_3, S1.Pin_4, R2.Pin_0

custom parts:
  NRF24L01: NRF24L01 module
