# Fritzing sketch Circuit Schematic (saved by Fritzing 0.8.7b)

parts:
  Raspberry_Pi_1 = Raspberry Pi 3 [part_number=RPI-3-V1.2]
  MD09B1 = A4988 Stepper Motor Driver Carrier
  M1 = Stepper Motor - Bipolar
  VCC1 = Battery block 9V

nets:
  N1: Raspberry_Pi_1.3v3, MD09B1.SLEEP
  N2: Raspberry_Pi_1.GND, MD09B1.GROUND#147
  N3: Raspberry_Pi_1.GIPO21, MD09B1.STEP
  N4: Raspberry_Pi_1.GIPO20, MD09B1.DIR
  N5: MD09B1.VMOT, VCC1.+
  N6: MD09B1.GROUND#141, VCC1.-
  N7: MD09B1.OUT_2B, M1.A
  N8: MD09B1.OUT_2A, M1.C
  N9: MD09B1.OUT_1A, M1.B
  N10: MD09B1.OUT_1B, M1.D
