# Fritzing sketch Circuit Diagram (saved by Fritzing 0.8.7b)
breadboards: 1

parts:
  Raspberry_Pi_B_rev1 = Raspberry Pi B rev2
  S7 = Pushbutton [package=THT]
  S8 = Pushbutton [package=THT]
  S9 = Pushbutton [package=THT]
  S10 = Pushbutton [package=THT]
  S11 = Pushbutton [package=THT]
  S12 = Pushbutton [package=THT]

nets:
  N1: Raspberry_Pi_B_rev1.GPIO_2, S12.leg1
  N2: Raspberry_Pi_B_rev1.GPIO_3, S11.leg1
  N3: Raspberry_Pi_B_rev1.GND, S7.leg0, S8.leg0, S9.leg0, S10.leg0, S11.leg0, S12.leg0
  N4: Raspberry_Pi_B_rev1.GPIO_17, S9.leg1
  N5: Raspberry_Pi_B_rev1.GPIO_27, S8.leg1
  N6: Raspberry_Pi_B_rev1.GPIO_22, S7.leg1
  N7: Raspberry_Pi_B_rev1.GPIO_4, S10.leg1
