# Fritzing sketch schematic (saved by Fritzing 0.8.7b)
breadboards: 1

parts:
  Raspberry_Pi_1 = Raspberry Pi 3 [part_number=RPI-3-V1.2]
  LED3 = RGB LED (com. cathode, rgb) [package="5 mm [THT]"]

nets:
  N1: Raspberry_Pi_1.GIPO17, LED3.red_anode
  N2: Raspberry_Pi_1.GIPO27, LED3.green_anode
  N3: Raspberry_Pi_1.GIPO22, LED3.blue_anode
  N4: Raspberry_Pi_1.GND, LED3.common_cathode
